# Fritzing sketch station_meteo (saved by Fritzing 0.9.3b)
breadboards: 1

parts:
  U1 = ESP32-38PinWide [part_number=ESP32-38PinWide]
  VCC1 = Battery
  Mod1 = KY-024 Linear Hall Magnetic Sensor Module [package="Breakout board"]
  Composant1 = Adafruit BME280 [part_number="Adafruit #2652"]
  Composant2 = BH1750
  R2 = Resistor [tolerance=±5% resistance=220 package=THT]
  R3 = Resistor [tolerance=±5% resistance=220 package=THT]
  R4 = Resistor [tolerance=±5% resistance=220 package=THT]
  OLED1 = OLED 128x64 I2C Monochrome Display GND-VDD
  U2 = WS2812 RGB LED strip
  F1 = Fan - 4 wire [package=THT]
  R5 = Resistor [tolerance=±5% resistance=220 package=THT]
  U3 = WS2812 RGB LED strip
  R6 = Resistor [tolerance=±5% resistance=220 package=THT]
  R7 = Resistor [tolerance=±5% resistance=220 package=THT]

nets:
  N1: U1.3.3, R6.Pin_0
  N2: U1.GPIO35, Mod1.A0
  N3: U1.GPIO32, Mod1.D0
  N4: U1.GPIO27, F1.PWM
  N5: U1.GPIO14, OLED1.SCK
  N6: U1.GND, U2.GND#0
  N7: U1.GPIO13, OLED1.SDA
  N8: U1.GPIO2, U2.DIN
  N9: U1.GPIO5, Composant1.CS
  N10: U1.GPIO18, Composant1.SCK/SCL
  N11: U1.GPIO19, Composant1.SDO/ADR
  N12: U1.GPIO21, Composant2.SDA
  N13: U1.GPIO22, Composant2.SCL
  N14: U1.GPIO23, Composant1.SDI/SDA
  GND: VCC1.-, Mod1.G, Composant1.GND, Composant2.GND, OLED1.GND, F1.GND
  N15: VCC1.+, R2.Pin_0, R3.Pin_0, R4.Pin_0, R5.Pin_0, R7.Pin_0
  N16: Mod1.+, R2.Pin_1
  N17: Composant1.VCC, R3.Pin_1
  N18: Composant2.VCC, R4.Pin_1
  N19: OLED1.VDD, R7.Pin_1
  N20: U2.VCC#1, R6.Pin_1
  N21: U2.GND#4, U3.GND
  N22: U2.VCC#5, U3.VCC
  N23: U2.DOUT, U3.DIN
  N24: F1.Power, R5.Pin_1

custom parts:
  ESP32-38PinWide: Generic 38-Pin ESP32 with wide format (only access to one side of pins on a breadboard) based on Stephen Lilley's HiLetgo ESP-WROOM-32 ESP32 ESP-32S Development Board.
  KY-024 Linear Hall Magnetic Sensor Module: KY-024 Linear Hall Magnetic Sensor Module reacts iin the presence of a magnetic field.
  Adafruit BME280: Bosch has stepped up their game with their new BME280 sensor, an environmental sensor with temperature, barometric pressure and humidity! This sensor is great for all sorts of indoor environmental sensing and can even be used in both I2C and SPI! This precision sensor from Bosch is the best low-cost sensing solution for measuring humidity with ±3% accuracy, barometric pressure with ±1 hPa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
  BH1750: Light Sensor
  OLED 128x64 I2C Monochrome Display GND-VDD: OLED 128x64 I2C Monochrome Display. Note: there are two variants of this part, this one is the GND VDD SCK SDA variant. The other is VDD GND SCK SDA. Make sure you select the part that matches your module as using the incorrect part will probably destroy your module! In addition the mounting holes are marked on silkscreen but not by default drilled. If you want drilled mounting holes, copy a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
  WS2812 RGB LED strip: WS2812 strip
  Fan - 4 wire: Fan, 4 wire with tach.
